// Logisim project Digital Clock Project.circ as structural Verilog: 10 circuits, main circuit main
module main (
  input  enable,
  input  clear
);

  wire and_1_out, and_2_out, clock_1_out, hour_all_1_h0_l, hour_all_1_h0_r, hour_all_1_h1_l, hour_all_1_h1_r,
       hour_all_1_h2_r, hour_all_1_h3_r, n7_segment_1_a_2, n7_segment_1_b_2, n7_segment_1_c_2,
       n7_segment_1_d_2, n7_segment_1_e, n7_segment_1_f, n7_segment_1_g, n7_segment_2_a_2, n7_segment_2_b_2,
       n7_segment_2_c_2, n7_segment_2_d_2, n7_segment_2_e, n7_segment_2_f, n7_segment_2_g, n7_segment_3_a_2,
       n7_segment_3_b_2, n7_segment_3_c_2, n7_segment_3_d_2, n7_segment_3_e, n7_segment_3_f, n7_segment_3_g,
       n7_segment_4_a_2, n7_segment_4_b_2, n7_segment_4_c_2, n7_segment_4_d_2, n7_segment_4_e,
       n7_segment_4_f, n7_segment_4_g, n7_segment_5_a_2, n7_segment_5_b_2, n7_segment_5_c_2,
       n7_segment_5_d_2, n7_segment_5_e, n7_segment_5_f, n7_segment_5_g, n7_segment_6_a_2, n7_segment_6_b_2,
       n7_segment_6_c_2, n7_segment_6_d_2, n7_segment_6_e, n7_segment_6_f, n7_segment_6_g, not_1_out,
       not_2_out, not_3_out, not_4_out, not_5_out, not_6_out, not_7_out, not_8_out, not_9_out,
       second_all_1_a0, second_all_1_a0_r, second_all_1_a1, second_all_1_a1_r, second_all_1_a2,
       second_all_1_a2_r, second_all_1_a3_r, second_all_2_a0, second_all_2_a0_r, second_all_2_a1,
       second_all_2_a1_r, second_all_2_a2, second_all_2_a2_r, second_all_2_a3_r;

  not not_1 (not_1_out, 1'b1);
  _7_segment u_7_segment_1 (
    .A(not_1_out), .B(not_1_out), .C(hour_all_1_h1_l), .D(hour_all_1_h0_l), .a_2(n7_segment_1_a_2),
    .b_2(n7_segment_1_b_2), .d_2(n7_segment_1_d_2), .c_2(n7_segment_1_c_2), .e(n7_segment_1_e),
    .f(n7_segment_1_f), .g(n7_segment_1_g));
  Hour_all hour_all_1 (
    .clear(clear), .clock(and_1_out), .enable(enable), .H3_R(hour_all_1_h3_r), .H1_L(hour_all_1_h1_l),
    .H2_R(hour_all_1_h2_r), .H0_L(hour_all_1_h0_l), .H1_R(hour_all_1_h1_r), .H0_R(hour_all_1_h0_r));
  _7_Segment_Display u_7_segment_display_1 (
    .g(n7_segment_1_g), .f(n7_segment_1_f), .a(n7_segment_1_a_2), .b(n7_segment_1_b_2), .e(n7_segment_1_e),
    .d(n7_segment_1_d_2), .c(n7_segment_1_c_2));  // open: dp
  _7_Segment_Display u_7_segment_display_2 (
    .g(n7_segment_2_g), .f(n7_segment_2_f), .a(n7_segment_2_a_2), .b(n7_segment_2_b_2), .e(n7_segment_2_e),
    .d(n7_segment_2_d_2), .c(n7_segment_2_c_2));  // open: dp
  and and_1 (and_1_out, not_2_out, not_4_out, not_3_out);
  _7_segment u_7_segment_2 (
    .A(hour_all_1_h3_r), .B(hour_all_1_h2_r), .C(hour_all_1_h1_r), .D(hour_all_1_h0_r),
    .a_2(n7_segment_2_a_2), .b_2(n7_segment_2_b_2), .d_2(n7_segment_2_d_2), .c_2(n7_segment_2_c_2),
    .e(n7_segment_2_e), .f(n7_segment_2_f), .g(n7_segment_2_g));
  not not_2 (not_2_out, second_all_1_a0);
  not not_3 (not_3_out, second_all_1_a2);
  not not_4 (not_4_out, second_all_1_a1);
  not not_5 (not_5_out, 1'b1);
  _7_segment u_7_segment_3 (
    .A(not_5_out), .B(second_all_1_a2), .C(second_all_1_a1), .D(second_all_1_a0), .a_2(n7_segment_3_a_2),
    .b_2(n7_segment_3_b_2), .d_2(n7_segment_3_d_2), .c_2(n7_segment_3_c_2), .e(n7_segment_3_e),
    .f(n7_segment_3_f), .g(n7_segment_3_g));
  _7_Segment_Display u_7_segment_display_3 (
    .g(n7_segment_3_g), .f(n7_segment_3_f), .a(n7_segment_3_a_2), .b(n7_segment_3_b_2), .e(n7_segment_3_e),
    .d(n7_segment_3_d_2), .c(n7_segment_3_c_2));  // open: dp
  Second_all second_all_1 (
    .clock(and_2_out), .enable(enable), .clear(clear), .A3_r(second_all_1_a3_r), .A2(second_all_1_a2),
    .A2_r(second_all_1_a2_r), .A1(second_all_1_a1), .A1_r(second_all_1_a1_r), .A0(second_all_1_a0),
    .A0_r(second_all_1_a0_r));
  _7_Segment_Display u_7_segment_display_4 (
    .g(n7_segment_4_g), .f(n7_segment_4_f), .a(n7_segment_4_a_2), .b(n7_segment_4_b_2), .e(n7_segment_4_e),
    .d(n7_segment_4_d_2), .c(n7_segment_4_c_2));  // open: dp
  and and_2 (and_2_out, not_8_out, not_7_out, not_6_out);
  _7_segment u_7_segment_4 (
    .A(second_all_1_a3_r), .B(second_all_1_a2_r), .C(second_all_1_a1_r), .D(second_all_1_a0_r),
    .a_2(n7_segment_4_a_2), .b_2(n7_segment_4_b_2), .d_2(n7_segment_4_d_2), .c_2(n7_segment_4_c_2),
    .e(n7_segment_4_e), .f(n7_segment_4_f), .g(n7_segment_4_g));
  not not_6 (not_6_out, second_all_2_a2);
  not not_7 (not_7_out, second_all_2_a1);
  not not_8 (not_8_out, second_all_2_a0);
  not not_9 (not_9_out, 1'b1);
  _7_segment u_7_segment_5 (
    .A(not_9_out), .B(second_all_2_a2), .C(second_all_2_a1), .D(second_all_2_a0), .a_2(n7_segment_5_a_2),
    .b_2(n7_segment_5_b_2), .d_2(n7_segment_5_d_2), .c_2(n7_segment_5_c_2), .e(n7_segment_5_e),
    .f(n7_segment_5_f), .g(n7_segment_5_g));
  Clock clock_1 (.out(clock_1_out));
  Second_all second_all_2 (
    .clock(clock_1_out), .enable(enable), .clear(clear), .A3_r(second_all_2_a3_r), .A2(second_all_2_a2),
    .A2_r(second_all_2_a2_r), .A1(second_all_2_a1), .A1_r(second_all_2_a1_r), .A0(second_all_2_a0),
    .A0_r(second_all_2_a0_r));
  _7_Segment_Display u_7_segment_display_5 (
    .g(n7_segment_5_g), .f(n7_segment_5_f), .a(n7_segment_5_a_2), .b(n7_segment_5_b_2), .e(n7_segment_5_e),
    .d(n7_segment_5_d_2), .c(n7_segment_5_c_2));  // open: dp
  _7_segment u_7_segment_6 (
    .A(second_all_2_a3_r), .B(second_all_2_a2_r), .C(second_all_2_a1_r), .D(second_all_2_a0_r),
    .a_2(n7_segment_6_a_2), .b_2(n7_segment_6_b_2), .d_2(n7_segment_6_d_2), .c_2(n7_segment_6_c_2),
    .e(n7_segment_6_e), .f(n7_segment_6_f), .g(n7_segment_6_g));
  _7_Segment_Display u_7_segment_display_6 (
    .g(n7_segment_6_g), .f(n7_segment_6_f), .a(n7_segment_6_a_2), .b(n7_segment_6_b_2), .e(n7_segment_6_e),
    .d(n7_segment_6_d_2), .c(n7_segment_6_c_2));  // open: dp

  // Notes on the sheet:
  //   ---------------------
  //   Hour
  //   |
  //   ---------------------
  //   |
  //   2107109
  //   |
  //   ---------------------
  //   Minute
  //   ---------------------
  //   2107110
  //   |
  //   |
  //   ---------------------
  //   Second
  //   |
  //   ---------------------
endmodule

module second_right (
  input  X,
  input  A3,
  input  A2,
  input  A1,
  input  A0,
  output D3,
  output D2,
  output D1,
  output D0
);

  wire and_1_out, and_2_out, and_3_out, and_4_out, and_5_out, and_6_out, and_7_out, and_8_out, not_1_out,
       not_2_out, not_3_out, not_4_out;

  not not_1 (not_1_out, A3);
  not not_2 (not_2_out, A1);
  not not_3 (not_3_out, A2);
  not not_4 (not_4_out, A0);
  and and_1 (and_1_out, A1, not_3_out, A0);
  and and_2 (and_2_out, A2, not_2_out);
  and and_3 (and_3_out, A2, not_4_out);
  and and_4 (and_4_out, A1, not_4_out);
  and and_5 (and_5_out, X, A3);
  and and_6 (and_6_out, A2, A0, A1);
  and and_7 (and_7_out, not_4_out, A3);
  and and_8 (and_8_out, A0, not_2_out, not_1_out);
  or or_1 (D3, and_6_out, and_7_out);
  or or_2 (D2, and_1_out, and_2_out, and_3_out);
  or or_3 (D1, and_8_out, and_4_out);
  or or_4 (D0, and_5_out, not_4_out);
endmodule

module second_left (
  input  A2,
  input  A1,
  input  A0,
  output D2,
  output D1,
  output D0,
  output Y
);

  wire and_1_out, and_2_out, and_3_out, and_4_out, not_1_out, not_2_out;

  not not_1 (not_1_out, A2);
  not not_2 (not_2_out, A1);
  not not_3 (D0, A0);
  and and_1 (and_1_out, A1, A0);
  and and_2 (and_2_out, D0, A2);
  and and_3 (and_3_out, not_1_out, not_2_out, A0);
  and and_4 (and_4_out, A1, D0);
  or or_1 (D2, and_1_out, and_2_out);
  or or_2 (D1, and_3_out, and_4_out);
  and and_5 (Y, A2, not_2_out, D0);
endmodule

module Skip (
  input  X,
  input  A3,
  input  A2,
  input  A1,
  input  A0,
  output clk
);

  wire and_1_out, and_2_out, not_1_out, not_2_out, not_3_out, not_4_out;

  not not_1 (not_1_out, A3);
  not not_2 (not_2_out, A1);
  not not_3 (not_3_out, A2);
  not not_4 (not_4_out, A0);
  and and_1 (and_1_out, not_4_out, not_2_out, not_3_out, not_1_out);
  and and_2 (and_2_out, A0, not_2_out, X, not_3_out, not_1_out);
  or or_1 (clk, and_1_out, and_2_out);
endmodule

module Second_all (
  input  clock,
  input  enable,
  input  clear,
  output A3_r,
  output A2,
  output A2_r,
  output A1,
  output A1_r,
  output A0,
  output A0_r
);

  wire second_left_1_d0, second_left_1_d1, second_left_1_d2, second_left_1_y, second_right_1_d0,
       second_right_1_d1, second_right_1_d2, second_right_1_d3, skip_1_clk;

  second_right second_right_1 (
    .X(second_left_1_y), .A3(A3_r), .A2(A2_r), .A1(A1_r), .A0(A0_r), .D3(second_right_1_d3),
    .D2(second_right_1_d2), .D1(second_right_1_d1), .D0(second_right_1_d0));
  D_Flip_Flop D3 (.clk(clock), .D(second_right_1_d3), .Q(A3_r), .en(enable), .reset(clear));  // open: Qn, preset
  D_Flip_Flop D2 (.clk(clock), .D(second_right_1_d2), .Q(A2_r), .en(enable), .reset(clear));  // open: Qn, preset
  D_Flip_Flop D1 (.clk(clock), .D(second_right_1_d1), .Q(A1_r), .en(enable), .reset(clear));  // open: Qn, preset
  D_Flip_Flop D0 (.clk(clock), .D(second_right_1_d0), .Q(A0_r), .en(enable), .reset(clear));  // open: Qn, preset
  Skip skip_1 (.X(second_left_1_y), .A3(A3_r), .A2(A2_r), .A1(A1_r), .A0(A0_r), .clk(skip_1_clk));
  D_Flip_Flop D2_2 (.clk(skip_1_clk), .D(second_left_1_d2), .Q(A2), .en(enable), .reset(clear));  // open: Qn, preset
  D_Flip_Flop D1_2 (.clk(skip_1_clk), .D(second_left_1_d1), .Q(A1), .en(enable), .reset(clear));  // open: Qn, preset
  D_Flip_Flop D0_2 (.clk(skip_1_clk), .D(second_left_1_d0), .Q(A0), .en(enable), .reset(clear));  // open: Qn, preset
  second_left second_left_1 (
    .A2(A2), .A1(A1), .A0(A0), .D2(second_left_1_d2), .D1(second_left_1_d1), .D0(second_left_1_d0),
    .Y(second_left_1_y));
endmodule

module _7_segment (
  input  A,
  input  B,
  input  C,
  input  D,
  output a_2,
  output b_2,
  output d_2,
  output c_2,
  output e,
  output f,
  output g
);

  wire and_1_out, and_2_out, and_3_out, and_4_out, and_5_out, and_6_out, and_7_out, and_8_out, and_9_out,
       not_1_out, not_2_out, not_3_out, not_4_out, not_5_out, or_1_out, or_2_out, or_3_out, or_4_out,
       or_5_out, or_9_out, or_10_out, or_11_out, or_12_out, xor_1_out, xor_2_out;

  not not_1 (not_1_out, B);
  not not_2 (not_2_out, C);
  not not_3 (not_3_out, D);
  or or_1 (or_1_out, A, C);
  xor xor_1 (xor_1_out, B, D);
  or or_2 (or_2_out, B, not_2_out);
  and and_1 (and_1_out, not_3_out, C);
  and and_2 (and_2_out, not_1_out, C);
  and and_3 (and_3_out, not_1_out, not_3_out);
  and and_4 (and_4_out, B, not_2_out);
  and and_5 (and_5_out, not_2_out, not_3_out);
  and and_6 (and_6_out, B, not_2_out);
  and and_7 (and_7_out, not_3_out, B);
  not not_4 (not_4_out, xor_1_out);
  not not_5 (not_5_out, xor_2_out);
  xor xor_2 (xor_2_out, C, D);
  or or_3 (or_3_out, and_2_out, and_3_out);
  and and_8 (and_8_out, and_4_out, D);
  or or_4 (or_4_out, and_5_out, and_6_out);
  and and_9 (and_9_out, B, not_3_out);
  or or_5 (or_5_out, and_9_out, A);
  or or_6 (a_2, or_1_out, not_4_out);
  or or_7 (b_2, not_1_out, not_5_out);
  or or_8 (c_2, or_2_out, D);
  or or_9 (or_9_out, and_1_out, A);
  or or_10 (or_10_out, or_3_out, and_8_out);
  or or_11 (or_11_out, and_6_out, and_2_out);
  or or_12 (or_12_out, and_7_out, A);
  or or_13 (d_2, or_9_out, or_10_out);
  or or_14 (e, and_1_out, and_3_out);
  or or_15 (f, or_4_out, or_5_out);
  or or_16 (g, or_11_out, or_12_out);
  _7_Segment_Display u_7_segment_display_1 (.g(g), .f(f), .a(a_2), .b(b_2), .e(e), .d(d_2), .c(c_2));  // open: dp
endmodule

module final_clock (
  input  enable,
  input  clear,
  input  in_3,
  input  in_4
);

  wire and_1_out, clock_1_out, n7_segment_1_a_2, n7_segment_1_b_2, n7_segment_1_c_2, n7_segment_1_d_2,
       n7_segment_1_e, n7_segment_1_f, n7_segment_1_g, n7_segment_2_a_2, n7_segment_2_b_2, n7_segment_2_c_2,
       n7_segment_2_d_2, n7_segment_2_e, n7_segment_2_f, n7_segment_2_g, n7_segment_3_a_2, n7_segment_3_b_2,
       n7_segment_3_c_2, n7_segment_3_d_2, n7_segment_3_e, n7_segment_3_f, n7_segment_3_g, n7_segment_4_a_2,
       n7_segment_4_b_2, n7_segment_4_c_2, n7_segment_4_d_2, n7_segment_4_e, n7_segment_4_f, n7_segment_4_g,
       not_1_out, not_2_out, not_3_out, second_all_1_a0, second_all_1_a0_r, second_all_1_a1,
       second_all_1_a1_r, second_all_1_a2, second_all_1_a2_r, second_all_1_a3_r, second_all_2_a0,
       second_all_2_a0_r, second_all_2_a1, second_all_2_a1_r, second_all_2_a2, second_all_2_a2_r,
       second_all_2_a3_r;

  _7_segment u_7_segment_1 (
    .A(in_3), .B(second_all_1_a2), .C(second_all_1_a1), .D(second_all_1_a0), .a_2(n7_segment_1_a_2),
    .b_2(n7_segment_1_b_2), .d_2(n7_segment_1_d_2), .c_2(n7_segment_1_c_2), .e(n7_segment_1_e),
    .f(n7_segment_1_f), .g(n7_segment_1_g));
  _7_Segment_Display u_7_segment_display_1 (
    .g(n7_segment_1_g), .f(n7_segment_1_f), .a(n7_segment_1_a_2), .b(n7_segment_1_b_2), .e(n7_segment_1_e),
    .d(n7_segment_1_d_2), .c(n7_segment_1_c_2));  // open: dp
  Second_all second_all_1 (
    .clock(and_1_out), .enable(enable), .clear(clear), .A3_r(second_all_1_a3_r), .A2(second_all_1_a2),
    .A2_r(second_all_1_a2_r), .A1(second_all_1_a1), .A1_r(second_all_1_a1_r), .A0(second_all_1_a0),
    .A0_r(second_all_1_a0_r));
  _7_Segment_Display u_7_segment_display_2 (
    .g(n7_segment_2_g), .f(n7_segment_2_f), .a(n7_segment_2_a_2), .b(n7_segment_2_b_2), .e(n7_segment_2_e),
    .d(n7_segment_2_d_2), .c(n7_segment_2_c_2));  // open: dp
  and and_1 (and_1_out, not_3_out, not_2_out, not_1_out);
  _7_segment u_7_segment_2 (
    .A(second_all_1_a3_r), .B(second_all_1_a2_r), .C(second_all_1_a1_r), .D(second_all_1_a0_r),
    .a_2(n7_segment_2_a_2), .b_2(n7_segment_2_b_2), .d_2(n7_segment_2_d_2), .c_2(n7_segment_2_c_2),
    .e(n7_segment_2_e), .f(n7_segment_2_f), .g(n7_segment_2_g));
  not not_1 (not_1_out, second_all_2_a2);
  not not_2 (not_2_out, second_all_2_a1);
  not not_3 (not_3_out, second_all_2_a0);
  _7_segment u_7_segment_3 (
    .A(in_4), .B(second_all_2_a2), .C(second_all_2_a1), .D(second_all_2_a0), .a_2(n7_segment_3_a_2),
    .b_2(n7_segment_3_b_2), .d_2(n7_segment_3_d_2), .c_2(n7_segment_3_c_2), .e(n7_segment_3_e),
    .f(n7_segment_3_f), .g(n7_segment_3_g));
  Clock clock_1 (.out(clock_1_out));
  Second_all second_all_2 (
    .clock(clock_1_out), .enable(enable), .clear(clear), .A3_r(second_all_2_a3_r), .A2(second_all_2_a2),
    .A2_r(second_all_2_a2_r), .A1(second_all_2_a1), .A1_r(second_all_2_a1_r), .A0(second_all_2_a0),
    .A0_r(second_all_2_a0_r));
  _7_Segment_Display u_7_segment_display_3 (
    .g(n7_segment_3_g), .f(n7_segment_3_f), .a(n7_segment_3_a_2), .b(n7_segment_3_b_2), .e(n7_segment_3_e),
    .d(n7_segment_3_d_2), .c(n7_segment_3_c_2));  // open: dp
  _7_segment u_7_segment_4 (
    .A(second_all_2_a3_r), .B(second_all_2_a2_r), .C(second_all_2_a1_r), .D(second_all_2_a0_r),
    .a_2(n7_segment_4_a_2), .b_2(n7_segment_4_b_2), .d_2(n7_segment_4_d_2), .c_2(n7_segment_4_c_2),
    .e(n7_segment_4_e), .f(n7_segment_4_f), .g(n7_segment_4_g));
  _7_Segment_Display u_7_segment_display_4 (
    .g(n7_segment_4_g), .f(n7_segment_4_f), .a(n7_segment_4_a_2), .b(n7_segment_4_b_2), .e(n7_segment_4_e),
    .d(n7_segment_4_d_2), .c(n7_segment_4_c_2));  // open: dp

  // Notes on the sheet:
  //   Minute
  //   Second
endmodule

module hourleft (
  input  A1,
  input  A0,
  output D1,
  output D0,
  output Y
);

  wire not_1_out, not_2_out;

  not not_1 (not_1_out, A1);
  not not_2 (not_2_out, A0);
  and and_1 (D0, not_1_out, not_2_out);
  and and_2 (Y, A1, not_2_out);

  assign D1 = A0;
endmodule

module hour_right (
  input  A0,
  input  A1,
  input  A2,
  input  A3,
  input  X,
  output D0,
  output D1,
  output D2,
  output D3
);

  wire and_1_out, and_2_out, and_3_out, and_4_out, and_5_out, and_6_out, and_7_out, not_2_out, not_3_out,
       not_4_out, not_5_out;

  not not_1 (D0, A0);
  not not_2 (not_2_out, A1);
  not not_3 (not_3_out, A2);
  not not_4 (not_4_out, A3);
  not not_5 (not_5_out, X);
  and and_1 (and_1_out, not_4_out, not_2_out, A0);
  and and_2 (and_2_out, A1, D0);
  and and_3 (and_3_out, not_5_out, not_3_out, A1, A0);
  and and_4 (and_4_out, A2, not_2_out);
  and and_5 (and_5_out, A2, D0);
  and and_6 (and_6_out, A2, A1, A0);
  and and_7 (and_7_out, A3, D0);
  or or_1 (D1, and_1_out, and_2_out);
  or or_2 (D2, and_3_out, and_4_out, and_5_out);
  or or_3 (D3, and_6_out, and_7_out);
endmodule

module Hour_all (
  input  clear,
  input  clock,
  input  enable,
  output H3_R,
  output H1_L,
  output H2_R,
  output H0_L,
  output H1_R,
  output H0_R
);

  wire and_1_out, hour_right_1_d0, hour_right_1_d1, hour_right_1_d2, hour_right_1_d3, hourleft_1_d0,
       hourleft_1_d1, hourleft_1_y, not_1_out, not_2_out, not_3_out, not_4_out;

  hour_right hour_right_1 (
    .A0(H0_R), .A1(H1_R), .A2(H2_R), .A3(H3_R), .X(hourleft_1_y), .D0(hour_right_1_d0), .D1(hour_right_1_d1),
    .D2(hour_right_1_d2), .D3(hour_right_1_d3));
  Clock clock_1 ();  // open: out
  D_Flip_Flop D3 (.clk(clock), .D(hour_right_1_d3), .Q(H3_R), .en(enable), .reset(clear));  // open: Qn, preset
  D_Flip_Flop D2 (.clk(clock), .D(hour_right_1_d2), .Q(H2_R), .en(enable), .reset(clear));  // open: Qn, preset
  D_Flip_Flop D1 (.clk(clock), .D(hour_right_1_d1), .Q(H1_R), .en(enable), .reset(clear));  // open: Qn, preset
  D_Flip_Flop D0 (.clk(clock), .D(hour_right_1_d0), .Q(H0_R), .en(enable), .reset(clear));  // open: Qn, preset
  not not_1 (not_1_out, H1_R);
  not not_2 (not_2_out, H0_R);
  not not_3 (not_3_out, H3_R);
  not not_4 (not_4_out, H2_R);
  and and_1 (and_1_out, not_3_out, not_4_out, not_1_out, not_2_out);
  D_Flip_Flop D1_2 (.clk(and_1_out), .D(hourleft_1_d1), .Q(H1_L), .en(enable), .reset(clear));  // open: Qn, preset
  D_Flip_Flop D0_2 (.clk(and_1_out), .D(hourleft_1_d0), .Q(H0_L), .en(enable), .reset(clear));  // open: Qn, preset
  hourleft hourleft_1 (.A1(H1_L), .A0(H0_L), .D1(hourleft_1_d1), .D0(hourleft_1_d0), .Y(hourleft_1_y));
endmodule
